# Fritzing sketch Arus (saved by Fritzing 0.9.6b)

parts:
  U1 = NodeMCU V3.0
  M1 = Pzem-004t
  LED1 = LEDs [package=led10mm]
  M2 = Pzem-004t

nets:
  N1: U1.D4, LED1.A
  N2: U1.D7, M1.RX, M2.RX
  N3: U1.D8, U1.RX, M1.TX, M2.TX
  GND: U1.GND, M1.GND, LED1.C, M2.GND
  N4: U1.VU, M1.5V

notes:
  0 - 250 V AC

custom parts:
  NodeMCU V3.0: ESP8266 based NodeMCU (modifed for Lolin 1.1 inch module, this one with the pcb reversed and schematic fixed up).
  Pzem-004t: Pzem-004t used for measuring AC voltage, current, active power, frequency, power factor and active energy, the module is without display function, the data is read through the TTL interface.
