# Fritzing sketch Base Diagram (saved by Fritzing 1.0.1rc)
circuit board: 10cm x 8cm

parts:
  U1 = JST XH 3A Male [chip_label=? package=THT]
  U2 = JST XH 4A 2.54mm [package=THT]
  U3 = JST-XH-6A
  U4 = LuaNode32 / ESP32 [part_number=ESP32S-PIN30]
  U5 = JST XH 4A 2.54mm [package=THT]
  U6 = JST XH 3A Male [chip_label=? package=THT]
  U8 = JST XH 3A Male [chip_label=? package=THT]
  U9 = JST XH 3A Male [chip_label=? package=THT]
  U10 = JST XH 3A Male [chip_label=? package=THT]
  U11 = JST XH 3A Male [chip_label=? package=THT]
  U12 = JST XH 3A Male [chip_label=? package=THT]
  U13 = JST XH 3A Male [chip_label=? package=THT]
  U14 = JST XH 3A Male [chip_label=? package=THT]
  J1 = female pin header, 15 pins [form="♀ (female)"]
  J2 = female pin header, 15 pins [form="♀ (female)"]
  U15 = JST XH 4A 2.54mm [package=THT]
  U16 = JST XH 4A 2.54mm [package=THT]
  U17 = JST XH 3A Male [chip_label=? package=THT]
  U18 = JST XH 4A 2.54mm [package=THT]
  U19 = JST XH 4A 2.54mm [package=THT]
  J3 = JST XH 2A male [form="♂ (male)" package=THT]
  J4 = male pin header, 3 pins [form="♂ (male)"]
  J5 = male pin header, 3 pins [form="♂ (male)"]

nets:
  N1: U1.pin1, U2.pin4, U3.pin6, U4.GND, U5.pin4, U6.pin1, U8.pin1, U9.pin1, U10.pin1, U11.pin1, U12.pin1, U13.pin1, U14.pin1, J1.pin2, J2.pin2, U15.pin4, U16.pin4, U17.pin1, U18.pin1, U19.pin1, J3.pin1, J4.pin1, J4.pin2, J4.pin3
  N2: U1.pin2, U2.pin3, U3.pin5, U4.Vin, U5.pin3, U6.pin2, U8.pin2, U9.pin2, U10.pin2, U11.pin2, U12.pin2, U13.pin2, U14.pin2, J2.pin1, U15.pin3, U16.pin3, U17.pin2, U18.pin2, U19.pin2, J3.pin2
  N3: U1.pin3, U4.D32, J2.pin10
  N4: U2.pin1, U4.D22, U5.pin1, J1.pin14, U15.pin1, U16.pin1
  N5: U2.pin2, U4.D21, U5.pin2, J1.pin11, U15.pin2, U16.pin2
  N6: U3.pin1, U4.D5, J1.pin8
  N7: U3.pin2, U4.D18, J1.pin9
  N8: U3.pin3, U4.D23, J1.pin15
  N9: U3.pin4, U4.D19, J1.pin10
  N10: U4.EN, J2.pin15
  N11: U4.VP, J2.pin14
  N12: U4.VN, J2.pin13
  N13: U4.D34, U8.pin3, J2.pin12
  N14: U4.D35, U6.pin3, J2.pin11
  N15: U4.D33, U10.pin3, J2.pin9
  N16: U4.D25, U9.pin3, J2.pin8
  N17: U4.D26, U11.pin3, J2.pin7
  N18: U4.D27, U12.pin3, J2.pin6
  N19: U4.D14, U13.pin3, J2.pin5
  N20: U4.D12, U14.pin3, J2.pin4
  N21: U4.D13, J2.pin3, U17.pin3
  N22: U4.3V3, J1.pin1, J5.pin1, J5.pin2, J5.pin3
  N23: U4.D15, J1.pin3
  N24: U4.D2, J1.pin4
  N25: U4.D4, J1.pin5
  N26: U4.RX2, J1.pin6, U19.pin3
  N27: U4.TX2, J1.pin7, U19.pin4
  N28: U4.RX0, J1.pin12, U18.pin3
  N29: U4.TX0, J1.pin13, U18.pin4

notes:
  JST 2.54 mm
  ESP32 DEVKIT V1 30 PIN

custom parts:
  JST XH 3A Male: 2.54 Mm JST "XH" connector
  JST XH 4A 2.54mm: 4 Pin JST XH connector
  JST-XH-6A: JST XH 6A (2.54)
  LuaNode32 / ESP32: New Image for LuaNode32 DOIT ESP32 DEVKIT V1. Base parts from LuaNode32 / ESP32 ESP32 based LuaNode32 by G.Noorlander DOIT Esp32 DevKit v1 (30 pins long, 11 pins width) by Werner Rothschopf (modified by vanepp Dec 2018)
  JST XH 2A male: JST XH-2A
