# Fritzing sketch Counter (saved by Fritzing 1.0.1rc)
circuit board: 8.46667cm x 5.64444cm

parts:
  Part1 = LCD1602-I2C
  Mod1 = Full Size SD Card Module
  RTC1 = DS3231 AT24C32 Real Time Clock
  S1 = Momentary Switch [package=ksa_sealed_tac_switch]
  S2 = Momentary Switch [package=ksa_sealed_tac_switch]
  S3 = Momentary Switch [package=ksa_sealed_tac_switch]
  IR1 = TSOP312.., 314.. [package=THT]
  U1 = LuaNode32 / ESP32 [part_number=ESP32S-PIN30]

nets:
  GND: Part1.GND, Mod1.pin_2, Mod1.pin_15, RTC1.GND
  VCC: Part1.VCC, RTC1.VCC, IR1.Vs, U1.Vin
  N1: Part1.SDA, RTC1.SDA, U1.D21
  N2: Part1.SCL, RTC1.SCL, U1.D22
  N3: Mod1.pin_4, U1.3V3
  N4: Mod1.pin_8, U1.D5
  N5: Mod1.pin_10, U1.D23
  N6: Mod1.pin_12, U1.D18
  N7: Mod1.pin_14, U1.D19
  N8: S1.1, U1.D34
  GND_2: S1.4, S2.4, S3.4, IR1.GND, U1.GND
  N9: S2.1, U1.D35
  N10: S3.1, U1.D32
  N11: IR1.Data, U1.D25

custom parts:
  LCD1602-I2C: A standard character display, usually with 2x16 characters. Comes in many colors with LCM1602 IIC attached.
  Full Size SD Card Module: SD Card Module Slot Socket Reader For Arduino ARM MCU
  DS3231 AT24C32 Real Time Clock: Real-time clock basedo on chip DS3231, plus memory chip AT24C32 (32 Kb storage capacity). On-chip temperature sensor with an accuracy of ±3 ℃, I2C bus interface maximum speed: 400 kHz. Operating voltage: 3.3 V to 5.5 V with battery backup capabilities.
  LuaNode32 / ESP32: New Image for LuaNode32 DOIT ESP32 DEVKIT V1. Base parts from LuaNode32 / ESP32 ESP32 based LuaNode32 by G.Noorlander DOIT Esp32 DevKit v1 (30 pins long, 11 pins width) by Werner Rothschopf (modified by vanepp Dec 2018)
