# Fritzing sketch Fuel Level (saved by Fritzing 1.0.1rc)

parts:
  U1 = LuaNode32 / ESP32 [part_number=ESP32S-PIN30]
  M1 = pt100 RTD
  Mod1 = Full Size SD Card Module
  U2 = LM2596 step down module
  SIM800L1 = SIM800L

nets:
  GND: U1.D26, U1.GND, M1.pin1, M1.pin2, Mod1.pin_1, Mod1.pin_2, U2.IN-, U2.OUT-, SIM800L1.GND
  VIN: U1.Vin, M1.pin3, Mod1.pin_5, Mod1.pin_6, U2.IN+, SIM800L1.VCC
  N1: U1.RX2, SIM800L1.TXD
  N2: U1.TX2, SIM800L1.RXD
  N3: U1.D5, Mod1.pin_7, Mod1.pin_8
  N4: U1.D18, Mod1.pin_11, Mod1.pin_12
  N5: U1.D19, Mod1.pin_13, Mod1.pin_14
  N6: U1.D23, Mod1.pin_9, Mod1.pin_10

custom parts:
  LuaNode32 / ESP32: New Image for LuaNode32 DOIT ESP32 DEVKIT V1. Base parts from LuaNode32 / ESP32 ESP32 based LuaNode32 by G.Noorlander DOIT Esp32 DevKit v1 (30 pins long, 11 pins width) by Werner Rothschopf (modified by vanepp Dec 2018)
  pt100 RTD: CrocSee RTD Pt100 Temperature Sensor Probe 3 Wires 2M Cable Thermocouple -58~572°F (-50-300°C) 1/2" BSP Thread.
  Full Size SD Card Module: SD Card Module Slot Socket Reader For Arduino ARM MCU
  LM2596 step down module: LM2596 DC-DC step down power supply module 3 A.
  SIM800L: SIM800L is a miniature cellular module which allows for GPRS transmission, sending and receiving SMS and making and receiving voice calls. Low cost and small footprint and quad band frequency support make this module perfect solution for any project that require long range connectivity. After connecting power module boots up, searches for cellular network and login automatically. On board LED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
