# Fritzing sketch GPS (saved by Fritzing 0.9.6b)

parts:
  U1 = LuaNode32 / ESP32 [part_number=ESP32S-PIN30]
  SIM800L1 = SIM800L
  U2 = NEO 6M GPS
  U3 = LM2596 step down module

nets:
  GND: U1.GND, SIM800L1.GND, U2.GND, U3.IN-, U3.OUT-
  VIN: U1.Vin, U2.VCC
  N1: U1.RX2, U2.TXD
  N2: U1.TX2, U2.RXD
  N3: U1.RX0, SIM800L1.TXD
  N4: U1.TX0, SIM800L1.RXD
  N5: SIM800L1.VCC, U3.OUT+

notes:
  IN 5-24 V DC
  OUT 4,1 - 4,2 V DC 2A

custom parts:
  LuaNode32 / ESP32: New Image for LuaNode32 DOIT ESP32 DEVKIT V1. Base parts from LuaNode32 / ESP32 ESP32 based LuaNode32 by G.Noorlander DOIT Esp32 DevKit v1 (30 pins long, 11 pins width) by Werner Rothschopf (modified by vanepp Dec 2018)
  SIM800L: SIM800L is a miniature cellular module which allows for GPRS transmission, sending and receiving SMS and making and receiving voice calls. Low cost and small footprint and quad band frequency support make this module perfect solution for any project that require long range connectivity. After connecting power module boots up, searches for cellular network and login automatically. On board LED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
  NEO 6M GPS: uSD module
  LM2596 step down module: LM2596 DC-DC step down power supply module 3 A.
