# Fritzing sketch RFID (saved by Fritzing 0.9.6b)

parts:
  U1 = LuaNode32 / ESP32 [part_number=ESP32S-PIN30]
  RTC1 = DS3231 AT24C32 Real Time Clock
  U2 = RELAY [package=relay-jzc]
  J1 = Camdenboss CTB0158-2 [part_number=CTB0158-2 package=THT]
  LED1 = LEDs [package=led10mm]
  LED2 = LEDs [package=led10mm]
  LED3 = LEDs [package=led10mm]
  R1 = Resistor [tolerance=±5% resistance=220 package="0603 [SMD]"]
  J2 = Infrared Proximity Sensor
  Mod1 = Full Size SD Card Module

nets:
  N1: U1.D34, U2.COIL1
  N2: U1.D35, LED2.C
  N3: U1.D32, LED3.C
  N4: U1.D33, LED1.C
  N5: U1.D13, J2.Vout
  GND: U1.GND, RTC1.GND, U2.MAIN, R1.Pin_1, J2.GND, Mod1.pin_2
  VIN: U1.Vin, J2.Vcc, Mod1.pin_5
  3V3: U1.3V3, RTC1.VCC
  N6: U1.D5, Mod1.pin_7
  N7: U1.D18, Mod1.pin_11
  N8: U1.D19, Mod1.pin_13
  N9: U1.D21, RTC1.SDA
  N10: U1.D22, RTC1.SCL
  N11: U1.D23, Mod1.pin_9
  N12: U2.COIL2, J1.pin2
  N13: U2.NC, J1.pin1
  N14: LED1.A, LED2.A, LED3.A, R1.Pin_0

custom parts:
  LuaNode32 / ESP32: New Image for LuaNode32 DOIT ESP32 DEVKIT V1. Base parts from LuaNode32 / ESP32 ESP32 based LuaNode32 by G.Noorlander DOIT Esp32 DevKit v1 (30 pins long, 11 pins width) by Werner Rothschopf (modified by vanepp Dec 2018)
  DS3231 AT24C32 Real Time Clock: Real-time clock basedo on chip DS3231, plus memory chip AT24C32 (32 Kb storage capacity). On-chip temperature sensor with an accuracy of ±3 ℃, I2C bus interface maximum speed: 400 kHz. Operating voltage: 3.3 V to 5.5 V with battery backup capabilities.
  Full Size SD Card Module: SD Card Module Slot Socket Reader For Arduino ARM MCU
