# Fritzing sketch Sensor Suhu Ruangan (saved by Fritzing 1.0.1rc)

parts:
  Part1 = LCD1602-I2C
  M1 = pt100 RTD
  U2 = LuaNode32 / ESP32 [part_number=ESP32S-PIN30]
  R1 = Rotary Potentiometer (Large) [maximum_resistance=100kΩ knob_status=50% package=THT]
  U3 = LM2596 step down module

nets:
  GND: Part1.GND, M1.pin1, M1.pin2, U2.D27, U2.GND, R1.leg2, U3.IN-, U3.OUT-
  VCC: Part1.VCC, M1.pin3, U2.Vin, R1.leg1, U3.OUT+
  N1: Part1.SDA, U2.D21
  N2: Part1.SCL, U2.D22
  N3: U2.D26, R1.wiper

notes:
  Adaptor 5-22 V DC

custom parts:
  LCD1602-I2C: A standard character display, usually with 2x16 characters. Comes in many colors with LCM1602 IIC attached.
  pt100 RTD: CrocSee RTD Pt100 Temperature Sensor Probe 3 Wires 2M Cable Thermocouple -58~572°F (-50-300°C) 1/2" BSP Thread.
  LuaNode32 / ESP32: New Image for LuaNode32 DOIT ESP32 DEVKIT V1. Base parts from LuaNode32 / ESP32 ESP32 based LuaNode32 by G.Noorlander DOIT Esp32 DevKit v1 (30 pins long, 11 pins width) by Werner Rothschopf (modified by vanepp Dec 2018)
  LM2596 step down module: LM2596 DC-DC step down power supply module 3 A.
