# Fritzing sketch Sensor Tangki Minyak (saved by Fritzing 1.0.5)

parts:
  U1 = LuaNode32 / ESP32 [part_number=ESP32S-PIN30]
  A1 = DFR Sen0313
  A2 = max485 cd4069 module
  U2 = LM2596 step down module

nets:
  N1: U1.GND, A1.Pin_2, A2.Pin_4, A2.Pin_5, U2.IN-, U2.OUT-
  N2: U1.Vin, A1.Pin_1, A2.Pin_1, U2.OUT+
  N3: U1.RX2, A2.Pin_2
  N4: U1.TX2, A2.Pin_3
  N5: A1.Pin_3, A2.Pin_7
  N6: A1.Pin_4, A2.Pin_6

custom parts:
  LuaNode32 / ESP32: New Image for LuaNode32 DOIT ESP32 DEVKIT V1. Base parts from LuaNode32 / ESP32 ESP32 based LuaNode32 by G.Noorlander DOIT Esp32 DevKit v1 (30 pins long, 11 pins width) by Werner Rothschopf (modified by vanepp Dec 2018)
  DFR Sen0313: A01NYUB Waterproof Ultrasonic Distance Sensor (28~750cm, UART, IP67).
  max485 cd4069 module: Module,3.3V-5.5V 485 to Serial UART Level Mutual Conversion Hardware Automatic Flow Control Module.
  LM2596 step down module: LM2596 DC-DC step down power supply module 3 A.
