# Fritzing sketch Suhu Ruangan L (saved by Fritzing 1.0.1rc)

parts:
  U1 = LuaNode32 / ESP32 [part_number=ESP32S-PIN30]
  Part1 = LCD1602-I2C
  A1 = DHT22 module
  U3 = LM2596 step down module  # not connected
  LED1 = LED - 3mm [color="Red (633nm)" current=0.030 package="3 mm [THT]"]
  J1 = Piezo Speaker

nets:
  N1: U1.D32, LED1.cathode
  N2: U1.D33, J1.pin2
  N3: U1.D14, A1.Out
  GND: U1.GND, Part1.GND, A1.-, LED1.anode, J1.pin1
  VIN: U1.Vin, Part1.VCC, A1.+
  N4: U1.D21, Part1.SDA
  N5: U1.D22, Part1.SCL

notes:
  DHT21
  OUT: Micro USB ESP32
  IN: Adaptor 6-24 V DC
  Buzzer
  LED
  LCD 16x2 I2C
  ESP32 Doit V1

custom parts:
  LuaNode32 / ESP32: New Image for LuaNode32 DOIT ESP32 DEVKIT V1. Base parts from LuaNode32 / ESP32 ESP32 based LuaNode32 by G.Noorlander DOIT Esp32 DevKit v1 (30 pins long, 11 pins width) by Werner Rothschopf (modified by vanepp Dec 2018)
  LCD1602-I2C: A standard character display, usually with 2x16 characters. Comes in many colors with LCM1602 IIC attached.
  DHT22 module: DHT22 module. Pins VCC Data GND.
  LM2596 step down module: LM2596 DC-DC step down power supply module 3 A.
