# Fritzing sketch Suhu Ruangan (saved by Fritzing 1.0.1rc)

parts:
  U1 = LuaNode32 / ESP32 [part_number=ESP32S-PIN30]
  Part1 = LCD1602-I2C
  U2 = POT [knob_status=50% package=pot_mammoth]
  A1 = DHT22 module
  U3 = LM2596 step down module  # not connected

nets:
  N1: U1.D34, U2.A
  N2: U1.D14, A1.Out
  GND: U1.GND, Part1.GND, U2.S, A1.-
  VIN: U1.Vin, Part1.VCC, A1.+
  N3: U1.3V3, U2.E
  N4: U1.D21, Part1.SDA
  N5: U1.D22, Part1.SCL

notes:
  Potensiometer
  100K Ohm
  DHT21
  OUT: Micro USB ESP32
  IN: Adaptor 6-24 V DC

custom parts:
  LuaNode32 / ESP32: New Image for LuaNode32 DOIT ESP32 DEVKIT V1. Base parts from LuaNode32 / ESP32 ESP32 based LuaNode32 by G.Noorlander DOIT Esp32 DevKit v1 (30 pins long, 11 pins width) by Werner Rothschopf (modified by vanepp Dec 2018)
  LCD1602-I2C: A standard character display, usually with 2x16 characters. Comes in many colors with LCM1602 IIC attached.
  DHT22 module: DHT22 module. Pins VCC Data GND.
  LM2596 step down module: LM2596 DC-DC step down power supply module 3 A.
