# Fritzing sketch Suhu (saved by Fritzing 0.9.3b)

parts:
  U1 = ESP32S-HiLetgo [part_number=ESP32S-HiLetgo]
  A1 = nozzle-bolt style thermocouple [package=THT]
  A2 = MAX6675 module [package=THT]
  Part1 = LCD1602-I2C
  U2 = POT [package=pot_mammoth]

nets:
  N1: U1.GPIO32, U2.A
  N2: U1.GPIO11, U2.E
  N3: U1.VIN, U2.S
  N4: U1.GPIO6, A2.pin2, Part1.VCC
  N5: U1.GPIO7, A2.pin1, Part1.GND
  N6: U1.GPIO0, A2.pin3
  N7: U1.GPIO4, A2.pin4
  N8: U1.GPIO16, A2.pin5
  N9: U1.GPIO21, Part1.SDA
  N10: U1.GPIO22, Part1.SCL
  N11: A1.pin1, A2.pin7
  N12: A1.pin2, A2.pin6

custom parts:
  ESP32S-HiLetgo: HiLetgo ESP-WROOM-32 ESP32 ESP-32S Development Board 2.4GHz Dual-Mode WiFi + Bluetooth Dual Cores Microcontroller The ESP32 integrated with Antenna switches, RF Balun, power amplifiers, low-noise amplifiers, filters, and management modules, and the entire solution occupies the least area of PCB. 2.4 GHz Wi-Fi plus Bluetooth dual-mode chip, with TSMC Ultra-low power consumption 40nm technology,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
  nozzle-bolt style thermocouple: Generic nozzle-bolt style thermocouple.
  MAX6675 module: MAX6675 Module + K Type Thermocouple Sensor Temperature Degrees.
  LCD1602-I2C: A standard character display, usually with 2x16 characters. Comes in many colors with LCM1602 IIC attached.
