# Fritzing sketch Weigher (saved by Fritzing 1.0.1rc)

parts:
  U1 = LuaNode32 / ESP32 [part_number=ESP32S-PIN30]
  Mod1 = Full Size SD Card Module
  A1 = w5500 module
  U2 = LM2596 step down module
  Part1 = HX711 Weighing Sensor Module
  Load_Cell1 = Load Cell - Red/white/black/green
  Btn1 = Adafruit Push-button Power Switch Breakout [package=THT]
  Btn2 = Adafruit Push-button Power Switch Breakout [package=THT]
  Btn3 = Adafruit Push-button Power Switch Breakout [package=THT]
  Part2 = LCD1602-I2C

nets:
  N1: U1.D34, Btn1.OUT
  N2: U1.D35, Btn3.OUT
  N3: U1.D32, Btn2.OUT
  N4: U1.D26, Part1.DO/RX
  N5: U1.D27, Part1.CK/TX
  N6: U1.GND, U2.OUT-
  N7: U1.Vin, U2.OUT+
  N8: U1.D4, Mod1.pin_8
  N9: U1.D5, A1.Pin_5
  N10: U1.D18, Mod1.pin_11, Mod1.pin_12, A1.Pin_4
  N11: U1.D19, Mod1.pin_14, A1.Pin_7
  N12: U1.D21, Part2.SDA
  N13: U1.D22, Part2.SCL
  N14: U1.D23, Mod1.pin_10, A1.Pin_3
  N15: Part1.E+, Load_Cell1.wire1
  N16: Part1.E-, Load_Cell1.wire2
  N17: Part1.A+, Load_Cell1.wire3
  N18: Part1.A-, Load_Cell1.wire4

custom parts:
  LuaNode32 / ESP32: New Image for LuaNode32 DOIT ESP32 DEVKIT V1. Base parts from LuaNode32 / ESP32 ESP32 based LuaNode32 by G.Noorlander DOIT Esp32 DevKit v1 (30 pins long, 11 pins width) by Werner Rothschopf (modified by vanepp Dec 2018)
  Full Size SD Card Module: SD Card Module Slot Socket Reader For Arduino ARM MCU
  w5500 module: MELIFE 3pcs W5500 SPI to LAN Ethernet Network Module TCP IP STM32 Interface 3.3V 5V Compatible with WIZ820io RC5.
  LM2596 step down module: LM2596 DC-DC step down power supply module 3 A.
  HX711 Weighing Sensor Module: HX711 is a precision 24-bit analog-to-digital converter (ADC) designed for weigh scales and industrial control applications to interface directly with a bridge sensor.
  Load Cell - Red/white/black/green: A rectangle load cell/weighting pressure Sensor with four wires - Red, white, black, green. Normally corresponding with E+, E-, A+, A- respectively.
  LCD1602-I2C: A standard character display, usually with 2x16 characters. Comes in many colors with LCM1602 IIC attached.
