# Fritzing sketch Molding (saved by Fritzing 0.9.6b)

parts:
  U1 = NodeMCU V3.0
  M1 = Pzem-004t
  LED1 = LEDs [package=led10mm]
  OMRON1 = OMRON PCB Power Relay – G5LE [part_number="G5LE-1\n" package=THT]
  J1 = Camdenboss CTB0158-2 [part_number=CTB0158-2 package=THT]

nets:
  N1: U1.D4, LED1.A
  N2: U1.D7, M1.RX
  N3: U1.D8, U1.RX, M1.TX
  GND: U1.GND, M1.GND, LED1.C
  N4: U1.VU, M1.5V
  N5: M1.LOUT, J1.terminal_1
  N6: M1.LIN, OMRON1.A
  N7: OMRON1.B, J1.terminal_2

notes:
  PLC 24 V DC
  0-220 V AC

custom parts:
  NodeMCU V3.0: ESP8266 based NodeMCU (modifed for Lolin 1.1 inch module, this one with the pcb reversed and schematic fixed up).
  Pzem-004t: Pzem-004t used for measuring AC voltage, current, active power, frequency, power factor and active energy, the module is without display function, the data is read through the TTL interface.
